# Fritzing sketch ESP8266_Temp_Sensor_Wiring_Diagram (saved by Fritzing 0.9.3b)

parts:
  U1 = ESP8266 NodeMCU LoLin module
  RHT1 = Humidity and Temperature Sensor RHT03
  part = Schottky Diode [part_number=1N5817 package="300 mil [THT]"]
  part_2 = Resistor [tolerance=±5% resistance=10k package=THT]

nets:
  N1: U1.D0, part.cathode
  N2: U1.D2, RHT1.Vcc, part_2.Pin_0
  N3: U1.GND, RHT1.GND_2
  N4: U1.RST, part.anode
  N5: RHT1.Data-signal, part_2.Pin_1

custom parts:
  ESP8266 NodeMCU LoLin module: ESP8266 based NodeMCU
